# Fritzing sketch button_hold_input (saved by Fritzing 0.9.2b)
breadboards: 1

parts:
  Part1 = Arduino Uno (Rev3)
  S2 = Pushbutton [package="[THT]"]
  R1 = Resistor [tolerance=±5% resistance=10k package=THT]

nets:
  N1: Part1.GND, R1.Pin_0
  N2: Part1.D2, S2.Pin_1, S2.Pin_2, R1.Pin_1
  N3: Part1.3V3, S2.Pin_3, S2.Pin_4
